// Logisim project Main.circ as structural Verilog: 5 circuits, main circuit main
module main (
);

  wire boot_controller_1_primer_ciclo, boot_controller_1_reloj, clock_1_out, switch_1_p2;
  wire [31:0] if_controller_1_indice, if_controller_1_instruccion;

  // Switch switch_1: pin names not known; wires that end beside it: 1'b1, switch_1_p2
  Pull_Resistor pull_resistor_1 (.node(switch_1_p2));
  Clock clock_1 (.out(clock_1_out));
  Boot_Controller boot_controller_1 (
    .Reloj_Externo(clock_1_out), .Interruptor(switch_1_p2), .Primer_Ciclo(boot_controller_1_primer_ciclo),
    .Reloj(boot_controller_1_reloj));
  Hex_Digit_Display #(.decimalPoint("false")) hex_digit_display_1 (.value(if_controller_1_instruccion[31:28]));
  Hex_Digit_Display #(.decimalPoint("false")) hex_digit_display_2 (.value(if_controller_1_indice[31:28]));
  IF_Controller if_controller_1 (
    .Indice_Salto({32{1'b0}}), .Saltar(1'b0), .Dormir(1'b0), .Reloj(boot_controller_1_reloj),
    .Reiniciar(boot_controller_1_primer_ciclo), .Usar_Little_Endian(1'b0), .Indice(if_controller_1_indice),
    .Instruccion(if_controller_1_instruccion));  // open: Doble_Instruccion, Media_Instruccion, Cuarto_Instruccion
  Hex_Digit_Display #(.decimalPoint("false")) hex_digit_display_3 (.value(if_controller_1_instruccion[27:24]));
  Hex_Digit_Display #(.decimalPoint("false")) hex_digit_display_4 (.value(if_controller_1_instruccion[23:20]));
  Hex_Digit_Display #(.decimalPoint("false")) hex_digit_display_5 (.value(if_controller_1_indice[27:24]));
  Hex_Digit_Display #(.decimalPoint("false")) hex_digit_display_6 (.value(if_controller_1_indice[23:20]));
  Hex_Digit_Display #(.decimalPoint("false")) hex_digit_display_7 (.value(if_controller_1_instruccion[19:16]));
  Hex_Digit_Display #(.decimalPoint("false")) hex_digit_display_8 (.value(if_controller_1_instruccion[15:12]));
  Hex_Digit_Display #(.decimalPoint("false")) hex_digit_display_9 (.value(if_controller_1_indice[19:16]));
  Hex_Digit_Display #(.decimalPoint("false")) hex_digit_display_10 (.value(if_controller_1_indice[15:12]));
  Hex_Digit_Display #(.decimalPoint("false")) hex_digit_display_11 (.value(if_controller_1_instruccion[11:8]));
  Hex_Digit_Display #(.decimalPoint("false")) hex_digit_display_12 (.value(if_controller_1_instruccion[7:4]));
  Hex_Digit_Display #(.decimalPoint("false")) hex_digit_display_13 (.value(if_controller_1_indice[11:8]));
  Hex_Digit_Display #(.decimalPoint("false")) hex_digit_display_14 (.value(if_controller_1_indice[7:4]));
  Hex_Digit_Display #(.decimalPoint("false")) hex_digit_display_15 (.value(if_controller_1_instruccion[3:0]));
  Hex_Digit_Display #(.decimalPoint("false")) hex_digit_display_16 (.value(if_controller_1_indice[3:0]));

  // Notes on the sheet:
  //   Encender computadora
endmodule

module Boot_Controller (
  input  Reloj_Externo,
  input  Interruptor,
  output Primer_Ciclo,
  output Reloj
);

  wire and_1_out, d_ff_1_q, d_ff_1_qn, not_1_out, t_ff_1_q, t_ff_1_qn;

  T_Flip_Flop t_ff_1 (
    .T(t_ff_1_qn), .clk(Reloj_Externo), .Q(t_ff_1_q), .Qn(t_ff_1_qn), .reset(not_1_out), .preset(1'b0));
  not not_1 (not_1_out, Interruptor);
  and and_1 (and_1_out, Reloj_Externo, Interruptor);
  and and_2 (Reloj, t_ff_1_q, and_1_out);
  D_Flip_Flop d_ff_1 (
    .D(t_ff_1_qn), .clk(Reloj_Externo), .Q(d_ff_1_q), .Qn(d_ff_1_qn), .preset(1'b0), .reset(not_1_out));
  // NoConnect on d_ff_1_qn
  and and_3 (Primer_Ciclo, d_ff_1_q, Reloj);
endmodule

module Four_GB_ROM_Controller (
  input  [31:0] Direccion_32_bits,
  input  Usar_Litte_Endian,
  output [63:0] Doubleword,
  output [31:0] Word,
  output [15:0] Nibble,
  output [7:0] Byte
);

  wire [2:0] subtractor_2_out;
  wire [31:0] multiplexer_1_out, subtractor_1_out;
  wire [63:0] multiplexer_2_out, multiplexer_3_out, rom_1_data, rom_2_data, rom_3_data, rom_4_data,
       rom_5_data, rom_6_data, rom_7_data, rom_8_data, rom_9_data, rom_10_data, rom_11_data, rom_12_data,
       rom_13_data, rom_14_data, rom_15_data, rom_16_data, rom_17_data, rom_18_data, rom_19_data,
       rom_20_data, rom_21_data, rom_22_data, rom_23_data, rom_24_data, rom_25_data, rom_26_data,
       rom_27_data, rom_28_data, rom_29_data, rom_30_data, rom_31_data, rom_32_data;

  Subtractor #(.width(32)) subtractor_1 (
    .a({32{1'b1}}), .b(Direccion_32_bits), .out(subtractor_1_out), .bin(1'b0));  // open: bout
  Multiplexer #(.width(32)) multiplexer_1 (
    .in0(Direccion_32_bits), .in1(subtractor_1_out), .out(multiplexer_1_out), .sel(Usar_Litte_Endian));
  Subtractor #(.width(3)) subtractor_2 (
    .a(3'b111), .b(multiplexer_1_out[2:0]), .out(subtractor_2_out), .bin(1'b0));  // open: bout
  ROM #(.addrWidth(24), .dataWidth(64)) rom_1 (.addr(multiplexer_1_out[26:3]), .data(rom_1_data));
  ROM #(.addrWidth(24), .dataWidth(64)) rom_2 (.addr(multiplexer_1_out[26:3]), .data(rom_2_data));
  ROM #(.addrWidth(24), .dataWidth(64)) rom_3 (.addr(multiplexer_1_out[26:3]), .data(rom_3_data));
  ROM #(.addrWidth(24), .dataWidth(64)) rom_4 (.addr(multiplexer_1_out[26:3]), .data(rom_4_data));
  ROM #(.addrWidth(24), .dataWidth(64)) rom_5 (.addr(multiplexer_1_out[26:3]), .data(rom_5_data));
  ROM #(.addrWidth(24), .dataWidth(64)) rom_6 (.addr(multiplexer_1_out[26:3]), .data(rom_6_data));
  ROM #(.addrWidth(24), .dataWidth(64)) rom_7 (.addr(multiplexer_1_out[26:3]), .data(rom_7_data));
  ROM #(.addrWidth(24), .dataWidth(64)) rom_8 (.addr(multiplexer_1_out[26:3]), .data(rom_8_data));
  ROM #(.addrWidth(24), .dataWidth(64)) rom_9 (.addr(multiplexer_1_out[26:3]), .data(rom_9_data));
  ROM #(.addrWidth(24), .dataWidth(64)) rom_10 (.addr(multiplexer_1_out[26:3]), .data(rom_10_data));
  ROM #(.addrWidth(24), .dataWidth(64)) rom_11 (.addr(multiplexer_1_out[26:3]), .data(rom_11_data));
  ROM #(.addrWidth(24), .dataWidth(64)) rom_12 (.addr(multiplexer_1_out[26:3]), .data(rom_12_data));
  ROM #(.addrWidth(24), .dataWidth(64)) rom_13 (.addr(multiplexer_1_out[26:3]), .data(rom_13_data));
  ROM #(.addrWidth(24), .dataWidth(64)) rom_14 (.addr(multiplexer_1_out[26:3]), .data(rom_14_data));
  ROM #(.addrWidth(24), .dataWidth(64)) rom_15 (.addr(multiplexer_1_out[26:3]), .data(rom_15_data));
  ROM #(.addrWidth(24), .dataWidth(64)) rom_16 (.addr(multiplexer_1_out[26:3]), .data(rom_16_data));
  ROM #(.addrWidth(24), .dataWidth(64)) rom_17 (.addr(multiplexer_1_out[26:3]), .data(rom_17_data));
  ROM #(.addrWidth(24), .dataWidth(64)) rom_18 (.addr(multiplexer_1_out[26:3]), .data(rom_18_data));
  ROM #(.addrWidth(24), .dataWidth(64)) rom_19 (.addr(multiplexer_1_out[26:3]), .data(rom_19_data));
  ROM #(.addrWidth(24), .dataWidth(64)) rom_20 (.addr(multiplexer_1_out[26:3]), .data(rom_20_data));
  ROM #(.addrWidth(24), .dataWidth(64)) rom_21 (.addr(multiplexer_1_out[26:3]), .data(rom_21_data));
  ROM #(.addrWidth(24), .dataWidth(64)) rom_22 (.addr(multiplexer_1_out[26:3]), .data(rom_22_data));
  ROM #(.addrWidth(24), .dataWidth(64)) rom_23 (.addr(multiplexer_1_out[26:3]), .data(rom_23_data));
  ROM #(.addrWidth(24), .dataWidth(64)) rom_24 (.addr(multiplexer_1_out[26:3]), .data(rom_24_data));
  ROM #(.addrWidth(24), .dataWidth(64)) rom_25 (.addr(multiplexer_1_out[26:3]), .data(rom_25_data));
  ROM #(.addrWidth(24), .dataWidth(64)) rom_26 (.addr(multiplexer_1_out[26:3]), .data(rom_26_data));
  ROM #(.addrWidth(24), .dataWidth(64)) rom_27 (.addr(multiplexer_1_out[26:3]), .data(rom_27_data));
  ROM #(.addrWidth(24), .dataWidth(64)) rom_28 (.addr(multiplexer_1_out[26:3]), .data(rom_28_data));
  ROM #(.addrWidth(24), .dataWidth(64)) rom_29 (.addr(multiplexer_1_out[26:3]), .data(rom_29_data));
  ROM #(.addrWidth(24), .dataWidth(64)) rom_30 (.addr(multiplexer_1_out[26:3]), .data(rom_30_data));
  ROM #(.addrWidth(24), .dataWidth(64)) rom_31 (.addr(multiplexer_1_out[26:3]), .data(rom_31_data));
  ROM #(.addrWidth(24), .dataWidth(64)) rom_32 (.addr(multiplexer_1_out[26:3]), .data(rom_32_data));
  Multiplexer #(.select(4), .width(64)) multiplexer_2 (
    .in0(rom_1_data), .in1(rom_2_data), .in2(rom_3_data), .in3(rom_4_data), .in4(rom_9_data),
    .in5(rom_10_data), .in6(rom_11_data), .in7(rom_12_data), .in8(rom_17_data), .in9(rom_18_data),
    .in10(rom_19_data), .in11(rom_20_data), .in12(rom_25_data), .in13(rom_26_data), .in14(rom_27_data),
    .in15(rom_28_data), .out(multiplexer_2_out), .sel(multiplexer_1_out[30:27]));
  Multiplexer #(.select(4), .width(64)) multiplexer_3 (
    .in0(rom_5_data), .in1(rom_6_data), .in2(rom_7_data), .in3(rom_8_data), .in4(rom_13_data),
    .in5(rom_14_data), .in6(rom_15_data), .in7(rom_16_data), .in8(rom_21_data), .in9(rom_22_data),
    .in10(rom_23_data), .in11(rom_24_data), .in12(rom_29_data), .in13(rom_30_data), .in14(rom_31_data),
    .in15(rom_32_data), .out(multiplexer_3_out), .sel(multiplexer_1_out[30:27]));
  Multiplexer #(.width(64)) multiplexer_4 (
    .in0(multiplexer_2_out), .in1(multiplexer_3_out), .out(Doubleword), .sel(multiplexer_1_out[31]));
  Multiplexer #(.width(32)) multiplexer_5 (
    .in0(Doubleword[31:0]), .in1(Doubleword[63:32]), .out(Word), .sel(subtractor_2_out[2]));
  Multiplexer #(.width(16)) multiplexer_6 (
    .in0(Word[15:0]), .in1(Word[31:16]), .out(Nibble), .sel(subtractor_2_out[1]));
  Multiplexer #(.width(8)) multiplexer_7 (.in0(Nibble[7:0]), .in1(Nibble[15:8]), .out(Byte), .sel(subtractor_2_out[0]));

  // Notes on the sheet:
  //   Tamaño de memoria accesible
  //   Longitud de byte
  //   contents of rom_1 (hex, n*v repeats v):
  //   123456789abcdef fedcba9876543210
  //   4 Gigabit
  //   4 Gigabit
  //   4 Gigabit
  //   4 Gigabit
  //   4 Gigabytes
  //   4 Giganibbles
  //   4 Giganibbles
  //   4 Gigabit
  //   4 Gigabit
  //   contents of rom_32 (hex, n*v repeats v):
  //   16777215*0 123456789abcdef
  //   4 Gigabit
  //   4 Gigabit
endmodule

module PC_Controller (
  input  [31:0] Indice_Salto,
  input  Tomar_Salto,
  input  Dormir,
  input  Reloj,
  input  Reiniciar,
  output [31:0] Indice
);

  wire not_1_out, not_2_out;
  wire [31:0] adder_1_out, multiplexer_1_out;

  not not_1 (not_1_out, Tomar_Salto);
  Multiplexer #(.width(32)) multiplexer_1 (
    .in0(Indice_Salto), .in1(adder_1_out), .out(multiplexer_1_out), .sel(not_1_out));
  not not_2 (not_2_out, Dormir);
  Register #(.width(32)) PC (.D(multiplexer_1_out), .en(not_2_out), .clk(Reloj), .Q(Indice), .clr(Reiniciar));
  Adder #(.width(32)) adder_1 (.a(32'h4), .b(Indice), .out(adder_1_out), .cin(1'b0));  // open: cout

  // Notes on the sheet:
  //   Alienamiento de Instrucciones
endmodule

module IF_Controller (
  input  [31:0] Indice_Salto,
  input  Saltar,
  input  Dormir,
  input  Reloj,
  input  Reiniciar,
  input  Usar_Little_Endian,
  output [31:0] Indice,
  output [63:0] Doble_Instruccion,
  output [31:0] Instruccion,
  output [15:0] Media_Instruccion,
  output [7:0] Cuarto_Instruccion
);

  PC_Controller pc_controller_1 (
    .Indice_Salto(Indice_Salto), .Tomar_Salto(Saltar), .Dormir(Dormir), .Reloj(Reloj), .Reiniciar(Reiniciar),
    .Indice(Indice));
  Four_GB_ROM_Controller four_gb_rom_controller_1 (
    .Direccion_32_bits(Indice), .Usar_Litte_Endian(Usar_Little_Endian), .Doubleword(Doble_Instruccion),
    .Word(Instruccion), .Nibble(Media_Instruccion), .Byte(Cuarto_Instruccion));
endmodule
